// Logisim project class_report_bp21042.circ as structural Verilog
module sel2_1 (
  input  C1,
  input  C2,
  input  SEL,
  output Y
);

  wire and_1_out, and_2_out, not_1_out;

  not not_1 (not_1_out, SEL);
  and and_1 (and_1_out, C1, not_1_out);
  and and_2 (and_2_out, SEL, C2);
  or or_1 (Y, and_1_out, and_2_out);
endmodule

module sel4_1 (
  input  C1,
  input  C2,
  input  C3,
  input  C4,
  input  SEL1,
  input  SEL0,
  output Y
);

  wire and_1_out, and_2_out, and_3_out, and_4_out, not_1_out, not_2_out, not_3_out, not_4_out;

  not not_1 (not_1_out, SEL1);
  not not_2 (not_2_out, SEL0);
  not not_3 (not_3_out, SEL1);
  not not_4 (not_4_out, SEL0);
  and and_1 (and_1_out, C1, not_1_out, not_2_out);
  and and_2 (and_2_out, C2, not_3_out, SEL0);
  and and_3 (and_3_out, C3, SEL1, not_4_out);
  and and_4 (and_4_out, C4, SEL1, SEL0);
  or or_1 (Y, and_1_out, and_2_out, and_3_out, and_4_out);
endmodule

module ALU_1 (
  input  A,
  input  B,
  input  SEL2,
  input  SEL3,
  output out_5
);

  wire and_1_out, not_1_out, or_1_out, xor_1_out;

  and and_1 (and_1_out, A, B);
  or or_1 (or_1_out, A, B);
  xor xor_1 (xor_1_out, A, B);
  not not_1 (not_1_out, A);
  sel4_1 sel4_1_1 (.C1(and_1_out), .C2(or_1_out), .C3(xor_1_out), .C4(not_1_out), .SEL1(SEL2), .SEL0(SEL3), .Y(out_5));
endmodule

module ALU_4 (
  input  A3,
  input  A2,
  input  A1,
  input  A0,
  input  B3,
  input  B2,
  input  B1,
  input  B0,
  input  SEL1,
  input  SEL2,
  output Z3,
  output Z2,
  output Z1,
  output Z0
);

  wire and_1_out, and_2_out, and_3_out, and_4_out, not_1_out, not_2_out, not_3_out, not_4_out, or_1_out,
       or_2_out, or_3_out, or_4_out, xor_1_out, xor_2_out, xor_3_out, xor_4_out;

  and and_1 (and_1_out, A3, B3);
  or or_1 (or_1_out, A3, B3);
  xor xor_1 (xor_1_out, A3, B3);
  not not_1 (not_1_out, A3);
  and and_2 (and_2_out, A2, B2);
  or or_2 (or_2_out, A2, B2);
  xor xor_2 (xor_2_out, A2, B2);
  not not_2 (not_2_out, A2);
  and and_3 (and_3_out, A1, B1);
  or or_3 (or_3_out, A1, B1);
  xor xor_3 (xor_3_out, A1, B1);
  not not_3 (not_3_out, A1);
  and and_4 (and_4_out, A0, B0);
  or or_4 (or_4_out, A0, B0);
  xor xor_4 (xor_4_out, A0, B0);
  not not_4 (not_4_out, A0);
  sel4_1 sel4_1_1 (.C1(and_1_out), .C2(or_1_out), .C3(xor_1_out), .C4(not_1_out), .SEL1(SEL1), .SEL0(SEL2), .Y(Z3));
  sel4_1 sel4_1_2 (.C1(and_2_out), .C2(or_2_out), .C3(xor_2_out), .C4(not_2_out), .SEL1(SEL1), .SEL0(SEL2), .Y(Z2));
  sel4_1 sel4_1_3 (.C1(and_3_out), .C2(or_3_out), .C3(xor_3_out), .C4(not_3_out), .SEL1(SEL1), .SEL0(SEL2), .Y(Z1));
  sel4_1 sel4_1_4 (.C1(and_4_out), .C2(or_4_out), .C3(xor_4_out), .C4(not_4_out), .SEL1(SEL1), .SEL0(SEL2), .Y(Z0));
endmodule

module HALF_ADDER (
  input  A,
  input  B,
  output sum,
  output carry
);

  xor xor_1 (sum, A, B);
  and and_1 (carry, A, B);
endmodule

module FULL_ADDER (
  input  A,
  input  B,
  input  ci,
  output sum,
  output cout
);

  wire and_1_out, and_2_out, xor_1_out;

  xor xor_1 (xor_1_out, A, B);
  xor xor_2 (sum, xor_1_out, ci);
  and and_1 (and_1_out, xor_1_out, ci);
  and and_2 (and_2_out, A, B);
  or or_1 (cout, and_1_out, and_2_out);
endmodule

module ADDER_4 (
  input  A3,
  input  A2,
  input  A1,
  input  A0,
  input  B3,
  input  B2,
  input  B1,
  input  B0,
  output Z3,
  output Z2,
  output Z1,
  output Z0,
  output overflow
);

  wire full_adder_1_cout, full_adder_2_cout, half_adder_1_carry;

  HALF_ADDER half_adder_1 (.A(A0), .B(B0), .sum(Z0), .carry(half_adder_1_carry));
  FULL_ADDER full_adder_1 (.A(A1), .B(B1), .ci(half_adder_1_carry), .sum(Z1), .cout(full_adder_1_cout));
  FULL_ADDER full_adder_2 (.A(A2), .B(B2), .ci(full_adder_1_cout), .sum(Z2), .cout(full_adder_2_cout));
  FULL_ADDER full_adder_3 (.A(A3), .B(B3), .ci(full_adder_2_cout), .sum(Z3), .cout(overflow));
endmodule

module COMPARATOR_2 (
  input  A1,
  input  A0,
  input  B1,
  input  B2
);
endmodule
